// Logisim project ALU control unit.circ as structural Verilog: 1 circuit, main circuit main
module main (
  input  [1:0] ALUOp,
  input  [5:0] Func,
  output [3:0] ALUCon
);

  wire and_1_out, and_2_out, and_3_out, not_1_out, not_2_out, or_1_out;

  not not_1 (not_1_out, Func[1]);
  not not_2 (not_2_out, Func[3]);
  and and_1 (and_1_out, Func[0], not_1_out, Func[2]);
  and and_2 (and_2_out, Func[1], Func[2], ALUOp[1], Func[0], not_2_out);
  or or_1 (or_1_out, and_1_out, Func[3]);
  and and_3 (and_3_out, ALUOp[1], Func[1]);
  and and_4 (ALUCon[0], ALUOp[1], or_1_out);
  nand nand_1 (ALUCon[1], ALUOp[1], Func[2]);
  or or_2 (ALUCon[2], ALUOp[0], and_3_out, and_2_out);
  and and_5 (ALUCon[3], ALUOp[1], Func[1], Func[2]);
endmodule
