// Logisim project ALU.circ as structural Verilog: 4 circuits, main circuit main
module main (
  input  Ainvert,
  input  Bnegate,
  input  [1:0] Operation,
  input  [31:0] Input_A,
  input  [31:0] Input_B,
  output [31:0] Result,
  output Zero
);

  wire [31:0] adder_1_out, and_1_out, n32_bit_2_way_multiplexer_1_output, n32_bit_2_way_multiplexer_2_output,
       not_1_out, not_2_out, or_1_out;

  assign not_1_out = ~Input_A;  // NOT_Gate not_1, 32 bits wide
  assign not_2_out = ~Input_B;  // NOT_Gate not_2, 32 bits wide
  _32_bit_2_way_multiplexer u_32_bit_2_way_multiplexer_1 (
    .Input_0(Input_A), .Input_1(not_1_out), .Selection_Bit_0(Ainvert),
    .Output(n32_bit_2_way_multiplexer_1_output));
  _32_bit_2_way_multiplexer u_32_bit_2_way_multiplexer_2 (
    .Input_0(Input_B), .Input_1(not_2_out), .Selection_Bit_0(Bnegate),
    .Output(n32_bit_2_way_multiplexer_2_output));
  Adder #(.width(32)) adder_1 (
    .a(n32_bit_2_way_multiplexer_1_output), .b(n32_bit_2_way_multiplexer_2_output), .out(adder_1_out),
    .cin(Bnegate));  // open: cout
  assign and_1_out = n32_bit_2_way_multiplexer_1_output & n32_bit_2_way_multiplexer_2_output;  // AND_Gate and_1, 32 bits wide
  assign or_1_out = n32_bit_2_way_multiplexer_1_output | n32_bit_2_way_multiplexer_2_output;  // OR_Gate or_1, 32 bits wide
  _32_bit_4_way_multiplexer u_32_bit_4_way_multiplexer_1 (
    .Input_0(and_1_out), .Input_1(or_1_out), .Input_2(adder_1_out), .Input_3({{31{1'b0}}, adder_1_out[31]}),
    .Selection_Bit_1(Operation[1]), .Selection_Bit_0(Operation[0]), .Output(Result));
  zero_logic zero_logic_1 (.\input (Result), .\output (Zero));
endmodule

module _32_bit_4_way_multiplexer (
  input  Selection_Bit_1,
  input  Selection_Bit_0,
  input  [31:0] Input_0,
  input  [31:0] Input_1,
  input  [31:0] Input_2,
  input  [31:0] Input_3,
  output [31:0] Output
);

  wire [31:0] and_1_out, and_2_out, and_3_out, and_4_out, not_1_out, not_2_out;

  assign not_1_out = ~{32{Selection_Bit_1}};  // NOT_Gate not_1, 32 bits wide
  assign not_2_out = ~{32{Selection_Bit_0}};  // NOT_Gate not_2, 32 bits wide
  assign and_1_out = not_2_out & Input_0 & not_1_out;  // AND_Gate and_1, 32 bits wide
  assign and_2_out = {32{Selection_Bit_0}} & Input_1 & not_1_out;  // AND_Gate and_2, 32 bits wide
  assign and_3_out = not_2_out & Input_2 & {32{Selection_Bit_1}};  // AND_Gate and_3, 32 bits wide
  assign and_4_out = {32{Selection_Bit_0}} & Input_3 & {32{Selection_Bit_1}};  // AND_Gate and_4, 32 bits wide
  assign Output = and_1_out | and_2_out | and_3_out | and_4_out;  // OR_Gate or_1, 32 bits wide
endmodule

module _32_bit_2_way_multiplexer (
  input  Selection_Bit_0,
  input  [31:0] Input_0,
  input  [31:0] Input_1,
  output [31:0] Output
);

  wire [31:0] and_1_out, and_2_out, not_1_out;

  assign not_1_out = ~{32{Selection_Bit_0}};  // NOT_Gate not_1, 32 bits wide
  assign and_1_out = Input_0 & not_1_out;  // AND_Gate and_1, 32 bits wide
  assign and_2_out = {32{Selection_Bit_0}} & Input_1;  // AND_Gate and_2, 32 bits wide
  assign Output = and_1_out | and_2_out;  // OR_Gate or_1, 32 bits wide
endmodule

module zero_logic (
  input  [31:0] \input ,
  output \output 
);

  wire or_1_out, or_2_out, or_3_out, or_4_out, or_5_out;

  or or_1 (or_1_out, \input [0], \input [1], \input [2], \input [3], \input [4], \input [5], \input [6], \input [7], \input [8]);
  or or_2 (or_2_out, \input [9], \input [10], \input [11], \input [12], \input [13], \input [14], \input [15]);
  or or_3 (or_3_out, \input [16], \input [17], \input [18], \input [19], \input [20], \input [21], \input [22]);
  or or_4 (or_4_out, \input [23], \input [24], \input [25], \input [26], \input [27], \input [28], \input [29], \input [30], \input [31]);
  not not_1 (\output , or_5_out);
  or or_5 (or_5_out, or_1_out, or_2_out, or_3_out, or_4_out);
endmodule
