// Logisim project main control unit.circ as structural Verilog: 1 circuit, main circuit main control unit
module main_control_unit (
  input  [5:0] opcode,
  output RegDst,
  output branch,
  output MemRead,
  output MemToReg,
  output [1:0] ALUOp,
  output MemWrite,
  output ALUSrc,
  output RegWrite
);

  wire not_1_out, not_2_out, not_3_out, not_4_out, not_5_out, not_6_out, not_7_out, not_8_out, not_9_out,
       not_10_out, not_11_out, not_12_out, not_13_out, not_14_out, not_15_out, not_16_out;

  not not_1 (not_1_out, opcode[3]);
  not not_2 (not_2_out, opcode[4]);
  not not_3 (not_3_out, opcode[5]);
  not not_4 (not_4_out, opcode[2]);
  not not_5 (not_5_out, opcode[0]);
  not not_6 (not_6_out, opcode[1]);
  and and_1 (ALUOp[1], not_3_out, not_2_out, not_1_out, not_4_out, not_6_out, not_5_out);
  not not_7 (not_7_out, opcode[3]);
  not not_8 (not_8_out, opcode[4]);
  and and_2 (MemRead, opcode[5], not_8_out, not_7_out, not_9_out, opcode[1], opcode[0]);
  not not_9 (not_9_out, opcode[2]);
  not not_10 (not_10_out, opcode[2]);
  not not_11 (not_11_out, opcode[4]);
  and and_3 (MemWrite, opcode[5], not_11_out, opcode[3], not_10_out, opcode[1], opcode[0]);
  not not_12 (not_12_out, opcode[3]);
  not not_13 (not_13_out, opcode[4]);
  not not_14 (not_14_out, opcode[5]);
  and and_4 (ALUOp[0], not_14_out, not_13_out, not_12_out, opcode[2], not_16_out, not_15_out);
  not not_15 (not_15_out, opcode[0]);
  not not_16 (not_16_out, opcode[1]);
  or or_1 (ALUSrc, MemRead, MemWrite);
  or or_2 (RegWrite, ALUOp[1], MemRead);

  assign branch = ALUOp[0];
  assign MemToReg = MemRead;
  assign RegDst = ALUOp[1];
endmodule
