// Logisim project multicyle_CPU.circ as structural Verilog: 4 circuits, main circuit main
module main (
);

  wire and_1_out, clock_1_out, main_2_zero, main_control_unit_1_alusrca, main_control_unit_1_irwrite,
       main_control_unit_1_lord, main_control_unit_1_memread, main_control_unit_1_memtoreg,
       main_control_unit_1_memwrite, main_control_unit_1_pcwrite, main_control_unit_1_pcwritecond,
       main_control_unit_1_regdst, main_control_unit_1_regwrite, or_1_out;
  wire [1:0] main_control_unit_1_aluop, main_control_unit_1_alusrcb, main_control_unit_1_pcsource;
  wire [3:0] main_1_alucon;
  wire [4:0] multiplexer_2_out;
  wire [5:0] Instruction_Register_q_2;
  wire [9:0] Instruction_Register_q_3;
  wire [27:0] PC_q;
  wire [31:0] A_q, ALUOut_q, B_q, left_shift_unit_1_out_2_2, left_shift_unit_2_out_2, main_2_result,
       Memory_Data_Register_q, multiplexer_1_out, multiplexer_3_out, multiplexer_4_out, multiplexer_5_out,
       multiplexer_6_out, n32_register_file_1_out_7, n32_register_file_1_out_8, ram_1_data,
       sing_extension_unit_1_out_2;
  wire [31:16] Instruction_Register_q;
  wire [31:28] left_shift_unit_1_out_2;

  Clock #(.highDuration(1), .lowDuration(1)) clock_1 (.out(clock_1_out));
  Register #(.width(32), .trigger("rising")) PC (
    .D(multiplexer_6_out), .en(or_1_out), .Q({left_shift_unit_1_out_2_2[31:28], PC_q}), .clk(clock_1_out));  // open: clr
  Multiplexer #(.select(1), .width(32)) multiplexer_1 (
    .in0({left_shift_unit_1_out_2_2[31:28], PC_q}), .in1(ALUOut_q), .out(multiplexer_1_out),
    .sel(main_control_unit_1_lord));
  or or_1 (or_1_out, and_1_out, main_control_unit_1_pcwrite);
  and and_1 (and_1_out, main_2_zero, main_control_unit_1_pcwritecond);
  RAM #(.addrWidth(6), .dataWidth(32), .bus("separate")) ram_1 (
    .addr(multiplexer_1_out[7:2]), .din(B_q), .data(ram_1_data), .str(main_control_unit_1_memwrite),
    .clk(clock_1_out), .ld(main_control_unit_1_memread));  // open: sel, clr
  Register #(.width(32), .trigger("rising")) Instruction_Register (
    .D(ram_1_data), .en(main_control_unit_1_irwrite),
    .Q({Instruction_Register_q, Instruction_Register_q_3, Instruction_Register_q_2}), .clk(clock_1_out));  // open: clr
  Register #(.width(32), .trigger("rising")) Memory_Data_Register (
    .D(ram_1_data), .Q(Memory_Data_Register_q), .clk(clock_1_out));  // open: en, clr
  main_control_unit main_control_unit_1 (
    .PCWriteCond(main_control_unit_1_pcwritecond), .PCWrite(main_control_unit_1_pcwrite),
    .lorD(main_control_unit_1_lord), .MemRead(main_control_unit_1_memread),
    .MemWrite(main_control_unit_1_memwrite), .MemToReg(main_control_unit_1_memtoreg),
    .IRWrite(main_control_unit_1_irwrite), .clock_input(clock_1_out), .Opcode(Instruction_Register_q[31:26]),
    .PCSource(main_control_unit_1_pcsource), .ALUOp(main_control_unit_1_aluop),
    .ALUSrcB(main_control_unit_1_alusrcb), .ALUSrcA(main_control_unit_1_alusrca),
    .RegWrite(main_control_unit_1_regwrite), .RegDst(main_control_unit_1_regdst));
  Multiplexer #(.select(1), .width(5)) multiplexer_2 (
    .in0(Instruction_Register_q[20:16]), .in1(Instruction_Register_q_3[9:5]), .out(multiplexer_2_out),
    .sel(main_control_unit_1_regdst));
  Multiplexer #(.select(1), .width(32)) multiplexer_3 (
    .in0(ALUOut_q), .in1(Memory_Data_Register_q), .out(multiplexer_3_out), .sel(main_control_unit_1_memtoreg));
  sing_extension_unit sing_extension_unit_1 (
    .in_1({Instruction_Register_q_3, Instruction_Register_q_2}), .out_2(sing_extension_unit_1_out_2));
  left_shift_unit left_shift_unit_1 (
    .in_1({{6{1'b0}}, Instruction_Register_q[25:16], Instruction_Register_q_3, Instruction_Register_q_2}),
    .out_2({left_shift_unit_1_out_2, left_shift_unit_1_out_2_2[27:0]}));
  _32_register_file u_32_register_file_1 (
    .in_1(Instruction_Register_q[25:21]), .in_2(Instruction_Register_q[20:16]), .in_3(multiplexer_2_out),
    .in_4(multiplexer_3_out), .Write(main_control_unit_1_regwrite), .clock(clock_1_out),
    .out_7(n32_register_file_1_out_7), .out_8(n32_register_file_1_out_8));
  Register #(.width(32), .trigger("rising")) A (
    .D(n32_register_file_1_out_7), .Q(A_q), .clk(clock_1_out));  // open: en, clr
  Register #(.width(32), .trigger("rising")) B (
    .D(n32_register_file_1_out_8), .Q(B_q), .clk(clock_1_out));  // open: en, clr
  left_shift_unit left_shift_unit_2 (.in_1(sing_extension_unit_1_out_2), .out_2(left_shift_unit_2_out_2));
  Multiplexer #(.select(1), .width(32)) multiplexer_4 (
    .in0({left_shift_unit_1_out_2_2[31:28], PC_q}), .in1(A_q), .out(multiplexer_4_out),
    .sel(main_control_unit_1_alusrca));
  Multiplexer #(.select(2), .width(32)) multiplexer_5 (
    .in0(B_q), .in1(32'h4), .in2(sing_extension_unit_1_out_2), .in3(left_shift_unit_2_out_2),
    .out(multiplexer_5_out), .sel(main_control_unit_1_alusrcb));
  ALU_control_unit_main main_1 (
    .ALUOp(main_control_unit_1_aluop), .Func(Instruction_Register_q_2), .ALUCon(main_1_alucon));
  ALU_main main_2 (
    .Input_A(multiplexer_4_out), .Input_B(multiplexer_5_out), .Ainvert(main_1_alucon[3]),
    .Bnegate(main_1_alucon[2]), .Operation(main_1_alucon[1:0]), .Result(main_2_result), .Zero(main_2_zero));
  Multiplexer #(.select(2), .width(32)) multiplexer_6 (
    .in0(main_2_result), .in1(ALUOut_q), .in2(left_shift_unit_1_out_2_2), .out(multiplexer_6_out),
    .sel(main_control_unit_1_pcsource));  // open: in3
  Register #(.width(32), .trigger("rising")) ALUOut (
    .D(main_2_result), .Q(ALUOut_q), .clk(clock_1_out));  // open: en, clr
endmodule

module sing_extension_unit (
  input  [15:0] in_1,
  output [31:0] out_2
);


  assign out_2 = {{17{in_1[15]}}, in_1[14:0]};
endmodule

module left_shift_unit (
  input  [31:0] in_1,
  output [31:0] out_2
);


  assign out_2 = {in_1[29:0], 2'b00};
endmodule

module main_control_unit (
  input  clock_input,
  input  [5:0] Opcode,
  output [1:0] PCSource,
  output PCWriteCond,
  output PCWrite,
  output [1:0] ALUOp,
  output lorD,
  output [1:0] ALUSrcB,
  output MemRead,
  output ALUSrcA,
  output MemWrite,
  output RegWrite,
  output MemToReg,
  output RegDst,
  output IRWrite
);

  wire [3:0] register_1_q, rom_1_data;

  Register #(.width(4), .trigger("rising")) register_1 (
    .D(rom_1_data), .Q(register_1_q), .clk(clock_input));  // open: en, clr
  ROM #(.addrWidth(10), .dataWidth(20)) rom_1 (
    .addr({Opcode, register_1_q}),
    .data({PCWrite, PCWriteCond, lorD, MemRead, MemWrite, IRWrite, MemToReg, PCSource, ALUOp, ALUSrcB, ALUSrcA, RegWrite, RegDst, rom_1_data}));  // open: sel

  // Notes on the sheet:
  //   contents of rom_1 (hex, n*v repeats v):
  //   1 94082 187 0 30005 2021 28001 448 31 40a41 81001 21*0 1 94082 18a 0 30005 2021 28001 448 31 40a41
  //   81001 21*0 1 94082 189 0 30005 2021 28001 448 31 40a41 81001 485*0 1 94082 183 144 30005 2021 28001
  //   448 31 40a41 81001 117*0 1 94082 183 146 30005 2021 28001 448 31 40a41 81001
endmodule
