// Logisim project register_file.circ as structural Verilog
module _4_register_section (
  input  [31:0] in_1,
  input  [3:0] dec_out,
  input  in_3,
  input  clock,
  output [31:0] out_5,
  output [31:0] out_6,
  output [31:0] out_7,
  output [31:0] out_8
);

  wire and_1_out, and_2_out, and_3_out, and_4_out, not_1_out, not_2_out, not_3_out, not_4_out, or_1_out,
       or_2_out, or_3_out, or_4_out;

  Register #(.width(32), .trigger("rising")) register_1 (.D(in_1), .Q(out_5), .clk(or_1_out));  // open: en, clr
  or or_1 (or_1_out, not_1_out, clock);
  and and_1 (and_1_out, dec_out[0], in_3);
  not not_1 (not_1_out, and_1_out);
  and and_2 (and_2_out, dec_out[1], in_3);
  Register #(.width(32), .trigger("rising")) register_2 (.D(in_1), .Q(out_6), .clk(or_2_out));  // open: en, clr
  or or_2 (or_2_out, not_2_out, clock);
  not not_2 (not_2_out, and_2_out);
  or or_3 (or_3_out, not_3_out, clock);
  not not_3 (not_3_out, and_3_out);
  and and_3 (and_3_out, dec_out[2], in_3);
  Register #(.width(32), .trigger("rising")) register_3 (.D(in_1), .Q(out_7), .clk(or_3_out));  // open: en, clr
  and and_4 (and_4_out, dec_out[3], in_3);
  Register #(.width(32), .trigger("rising")) register_4 (.D(in_1), .Q(out_8), .clk(or_4_out));  // open: en, clr
  or or_4 (or_4_out, not_4_out, clock);
  not not_4 (not_4_out, and_4_out);

  // Notes on the sheet:
  //   Write Enable
endmodule

module _32_register_file (
  input  [4:0] in_1,
  input  [4:0] in_2,
  input  [4:0] in_3,
  input  [31:0] in_4,
  input  Write,
  input  clock,
  output [31:0] out_7,
  output [31:0] out_8
);

  wire [31:0] n4_register_section_1_out_5, n4_register_section_1_out_6, n4_register_section_1_out_7,
       n4_register_section_1_out_8, n4_register_section_2_out_5, n4_register_section_2_out_6,
       n4_register_section_2_out_7, n4_register_section_2_out_8, n4_register_section_3_out_5,
       n4_register_section_3_out_6, n4_register_section_3_out_7, n4_register_section_3_out_8,
       n4_register_section_4_out_5, n4_register_section_4_out_6, n4_register_section_4_out_7,
       n4_register_section_4_out_8, n4_register_section_5_out_5, n4_register_section_5_out_6,
       n4_register_section_5_out_7, n4_register_section_5_out_8, n4_register_section_6_out_5,
       n4_register_section_6_out_6, n4_register_section_6_out_7, n4_register_section_6_out_8,
       n4_register_section_7_out_5, n4_register_section_7_out_6, n4_register_section_7_out_7,
       n4_register_section_7_out_8, n4_register_section_8_out_5, n4_register_section_8_out_6,
       n4_register_section_8_out_7, n4_register_section_8_out_8, n5_sel_decoder_1_out_2;

  _5_sel_decoder u_5_sel_decoder_1 (.in_1(in_3), .out_2(n5_sel_decoder_1_out_2));
  _4_register_section u_4_register_section_1 (
    .in_1(in_4), .dec_out(n5_sel_decoder_1_out_2[3:0]), .in_3(Write), .clock(clock),
    .out_5(n4_register_section_1_out_5), .out_6(n4_register_section_1_out_6),
    .out_7(n4_register_section_1_out_7), .out_8(n4_register_section_1_out_8));
  _4_register_section u_4_register_section_2 (
    .in_1(in_4), .dec_out(n5_sel_decoder_1_out_2[11:8]), .in_3(Write), .clock(clock),
    .out_5(n4_register_section_2_out_5), .out_6(n4_register_section_2_out_6),
    .out_7(n4_register_section_2_out_7), .out_8(n4_register_section_2_out_8));
  _4_register_section u_4_register_section_3 (
    .in_1(in_4), .dec_out(n5_sel_decoder_1_out_2[19:16]), .in_3(Write), .clock(clock),
    .out_5(n4_register_section_3_out_5), .out_6(n4_register_section_3_out_6),
    .out_7(n4_register_section_3_out_7), .out_8(n4_register_section_3_out_8));
  _4_register_section u_4_register_section_4 (
    .in_1(in_4), .dec_out(n5_sel_decoder_1_out_2[27:24]), .in_3(Write), .clock(clock),
    .out_5(n4_register_section_4_out_5), .out_6(n4_register_section_4_out_6),
    .out_7(n4_register_section_4_out_7), .out_8(n4_register_section_4_out_8));
  _4_register_section u_4_register_section_5 (
    .in_1(in_4), .dec_out(n5_sel_decoder_1_out_2[7:4]), .in_3(Write), .clock(clock),
    .out_5(n4_register_section_5_out_5), .out_6(n4_register_section_5_out_6),
    .out_7(n4_register_section_5_out_7), .out_8(n4_register_section_5_out_8));
  _4_register_section u_4_register_section_6 (
    .in_1(in_4), .dec_out(n5_sel_decoder_1_out_2[15:12]), .in_3(Write), .clock(clock),
    .out_5(n4_register_section_6_out_5), .out_6(n4_register_section_6_out_6),
    .out_7(n4_register_section_6_out_7), .out_8(n4_register_section_6_out_8));
  _4_register_section u_4_register_section_7 (
    .in_1(in_4), .dec_out(n5_sel_decoder_1_out_2[23:20]), .in_3(Write), .clock(clock),
    .out_5(n4_register_section_7_out_5), .out_6(n4_register_section_7_out_6),
    .out_7(n4_register_section_7_out_7), .out_8(n4_register_section_7_out_8));
  _4_register_section u_4_register_section_8 (
    .in_1(in_4), .dec_out(n5_sel_decoder_1_out_2[31:28]), .in_3(Write), .clock(clock),
    .out_5(n4_register_section_8_out_5), .out_6(n4_register_section_8_out_6),
    .out_7(n4_register_section_8_out_7), .out_8(n4_register_section_8_out_8));
  _5_sel_mux u_5_sel_mux_1 (
    .in_1(n4_register_section_1_out_5), .in_2(n4_register_section_1_out_6),
    .in_3(n4_register_section_1_out_7), .in_4(n4_register_section_1_out_8),
    .in_5(n4_register_section_5_out_5), .in_6(n4_register_section_5_out_6),
    .in_7(n4_register_section_5_out_7), .in_8(n4_register_section_5_out_8),
    .in_9(n4_register_section_2_out_5), .in_10(n4_register_section_2_out_6),
    .in_11(n4_register_section_2_out_7), .in_12(n4_register_section_2_out_8),
    .in_13(n4_register_section_6_out_5), .in_14(n4_register_section_6_out_6),
    .in_15(n4_register_section_6_out_7), .in_16(n4_register_section_6_out_8),
    .in_17(n4_register_section_3_out_5), .in_18(n4_register_section_3_out_6),
    .in_19(n4_register_section_3_out_7), .in_20(n4_register_section_3_out_8),
    .in_21(n4_register_section_7_out_5), .in_22(n4_register_section_7_out_6),
    .in_23(n4_register_section_7_out_7), .in_24(n4_register_section_7_out_8),
    .in_25(n4_register_section_4_out_5), .in_26(n4_register_section_4_out_6),
    .in_27(n4_register_section_4_out_7), .in_28(n4_register_section_4_out_8),
    .in_29(n4_register_section_8_out_5), .in_30(n4_register_section_8_out_6),
    .in_31(n4_register_section_8_out_7), .in_32(n4_register_section_8_out_8), .in_33(in_1), .out_34(out_7));
  _5_sel_mux u_5_sel_mux_2 (
    .in_1(n4_register_section_1_out_5), .in_2(n4_register_section_1_out_6),
    .in_3(n4_register_section_1_out_7), .in_4(n4_register_section_1_out_8),
    .in_5(n4_register_section_5_out_5), .in_6(n4_register_section_5_out_6),
    .in_7(n4_register_section_5_out_7), .in_8(n4_register_section_5_out_8),
    .in_9(n4_register_section_2_out_5), .in_10(n4_register_section_2_out_6),
    .in_11(n4_register_section_2_out_7), .in_12(n4_register_section_2_out_8),
    .in_13(n4_register_section_6_out_5), .in_14(n4_register_section_6_out_6),
    .in_15(n4_register_section_6_out_7), .in_16(n4_register_section_6_out_8),
    .in_17(n4_register_section_3_out_5), .in_18(n4_register_section_3_out_6),
    .in_19(n4_register_section_3_out_7), .in_20(n4_register_section_3_out_8),
    .in_21(n4_register_section_7_out_5), .in_22(n4_register_section_7_out_6),
    .in_23(n4_register_section_7_out_7), .in_24(n4_register_section_7_out_8),
    .in_25(n4_register_section_4_out_5), .in_26(n4_register_section_4_out_6),
    .in_27(n4_register_section_4_out_7), .in_28(n4_register_section_4_out_8),
    .in_29(n4_register_section_8_out_5), .in_30(n4_register_section_8_out_6),
    .in_31(n4_register_section_8_out_7), .in_32(n4_register_section_8_out_8), .in_33(in_2), .out_34(out_8));

  // Notes on the sheet:
  //   Read Sel0
  //   Read Sel1
  //   Write Sel
  //   Data
  //   Read Data 0
  //   Read Data 0
endmodule
