// Logisim project single_cyle_CPU.circ as structural Verilog: 2 circuits, main circuit main
module main (
);

  wire main_control_unit_1_alusrc, main_control_unit_1_regdst, main_control_unit_1_regwrite;
  wire [1:0] main_control_unit_1_aluop;
  wire [4:0] multiplexer_1_out;
  wire [31:0] multiplexer_2_out, n32_register_file_1_out_7, n32_register_file_1_out_8, ram_1_data,
       sing_extension_unit_1_out_2;

  RAM #(.addrWidth(7), .dataWidth(32), .bus("combined")) ram_1 (.data(ram_1_data));  // open: addr, sel, clk, ld, clr
  Multiplexer #(.select(1), .width(5)) multiplexer_1 (
    .in0(ram_1_data[20:16]), .in1(ram_1_data[15:11]), .out(multiplexer_1_out),
    .sel(main_control_unit_1_regdst));
  main_control_unit main_control_unit_1 (
    .opcode(ram_1_data[31:26]), .RegDst(main_control_unit_1_regdst), .ALUOp(main_control_unit_1_aluop),
    .ALUSrc(main_control_unit_1_alusrc), .RegWrite(main_control_unit_1_regwrite));  // open: branch, MemRead, MemToReg, MemWrite
  _32_register_file u_32_register_file_1 (
    .in_1(ram_1_data[25:21]), .in_2(ram_1_data[20:16]), .in_3(multiplexer_1_out),
    .Write(main_control_unit_1_regwrite), .out_7(n32_register_file_1_out_7), .out_8(n32_register_file_1_out_8));  // open: in_4, clock
  sing_extension_unit sing_extension_unit_1 (.in_1(ram_1_data[15:0]), .out_2(sing_extension_unit_1_out_2));
  Multiplexer #(.select(1), .width(32)) multiplexer_2 (
    .in0(n32_register_file_1_out_8), .in1(sing_extension_unit_1_out_2), .out(multiplexer_2_out),
    .sel(main_control_unit_1_alusrc));
  ALU_control_unit_main main_1 (.ALUOp(main_control_unit_1_aluop), .Func(ram_1_data[5:0]));  // open: ALUCon
  ALU_main main_2 (
    .Input_A(n32_register_file_1_out_7), .Input_B(multiplexer_2_out));  // open: Ainvert, Bnegate, Operation, Result, Zero
endmodule

module sing_extension_unit (
  input  [15:0] in_1,
  output [31:0] out_2
);


  assign out_2 = {{17{in_1[15]}}, in_1[14:0]};
endmodule
